# Fritzing sketch ElectricSchema (saved by Fritzing 0.9.3b)
breadboards: 1

parts:
  LED1 = RGB LED (com. cathode, rgb) [package="5 mm [THT]"]
  LED2 = RGB LED (com. cathode, rgb) [package="5 mm [THT]"]
  LED3 = RGB LED (com. cathode, rgb) [package="5 mm [THT]"]
  LED4 = RGB LED (com. cathode, rgb) [package="5 mm [THT]"]
  LED5 = RGB LED (com. cathode, rgb) [package="5 mm [THT]"]
  LED6 = RGB LED (com. cathode, rgb) [package="5 mm [THT]"]
  LED7 = RGB LED (com. cathode, rgb) [package="5 mm [THT]"]
  LED8 = RGB LED (com. cathode, rgb) [package="5 mm [THT]"]
  LED9 = RGB LED (com. cathode, rgb) [package="5 mm [THT]"]
  LED10 = RGB LED (com. cathode, rgb) [package="5 mm [THT]"]
  LED11 = RGB LED (com. cathode, rgb) [package="5 mm [THT]"]
  LED12 = RGB LED (com. cathode, rgb) [package="5 mm [THT]"]
  R1 = Resistor [tolerance=±5% resistance=1k package="1206 [SMD]"]
  R2 = Resistor [tolerance=±5% resistance=10k package="1206 [SMD]"]
  R3 = Resistor [tolerance=±5% resistance=1k package="1206 [SMD]"]
  R4 = Resistor [tolerance=±5% resistance=1k package="1206 [SMD]"]
  R5 = Resistor [tolerance=±5% resistance=1k package="1206 [SMD]"]
  R6 = Resistor [tolerance=±5% resistance=1k package="1206 [SMD]"]
  R7 = Resistor [tolerance=±5% resistance=1k package="1206 [SMD]"]
  Part1 = Arduino Uno (Rev3)
  S1 = Pushbutton [package="[SMD]"]
  R8 = Resistor [tolerance=±5% resistance=1k package="0603 [SMD]"]
  MOTOR1 = 28BYJ-48 Stepper Motor
  X1 = X113647 Stepper Driver Board [package=board]

nets:
  N1: LED1.red_anode, LED7.red_anode, R1.Pin_0
  GND: LED1.common_cathode, LED2.common_cathode, LED3.common_cathode, LED4.common_cathode, LED5.common_cathode, LED6.common_cathode, LED7.common_cathode, LED8.common_cathode, LED9.common_cathode, LED10.common_cathode, LED11.common_cathode, LED12.common_cathode, Part1.GND, R8.Pin_1, X1.GND
  N2: LED1.green_anode, LED7.green_anode, R2.Pin_0
  N3: LED1.blue_anode, LED7.blue_anode
  N4: LED2.red_anode, LED8.red_anode
  N5: LED2.green_anode, LED8.green_anode, R3.Pin_0
  N6: LED2.blue_anode, LED8.blue_anode
  N7: LED3.red_anode, LED9.red_anode
  N8: LED3.green_anode, LED9.green_anode, R4.Pin_0
  N9: LED3.blue_anode, LED9.blue_anode, R5.Pin_0
  N10: LED4.red_anode, LED10.red_anode
  N11: LED4.green_anode, LED10.green_anode
  N12: LED4.blue_anode, LED10.blue_anode, R6.Pin_0
  N13: LED5.red_anode, LED11.red_anode, Part1.D9_PWM
  N14: LED5.green_anode, LED11.green_anode
  N15: LED5.blue_anode, LED11.blue_anode, R7.Pin_0
  N16: LED6.red_anode, LED12.red_anode, Part1.D10_PWM/SS
  N17: LED6.green_anode, LED12.green_anode
  N18: LED6.blue_anode, LED12.blue_anode
  N19: R1.Pin_1, Part1.D2
  N20: R2.Pin_1, Part1.D3_PWM
  N21: R3.Pin_1, Part1.D4
  N22: R4.Pin_1, Part1.D5_PWM
  N23: R5.Pin_1, Part1.D6_PWM
  N24: R6.Pin_1, Part1.D7
  N25: R7.Pin_1, Part1.D8
  N26: Part1.A0, X1.IN4
  N27: Part1.A1, S1.Pin_1, S1.Pin_2, R8.Pin_0
  N28: Part1.D11_PWM/MOSI, X1.IN1
  N29: Part1.D12/MISO, X1.IN2
  N30: Part1.D13/SCK, X1.IN3
  N31: Part1.5V, S1.Pin_3, S1.Pin_4, X1.+V
  N32: MOTOR1.BLUE, X1.BLUE
  N33: MOTOR1.PINK, X1.PINK
  N34: MOTOR1.RED, X1.RED
  N35: MOTOR1.ORANGE, X1.ORANGE
  N36: MOTOR1.YELLOW, X1.YELLOW

custom parts:
  28BYJ-48 Stepper Motor: 28BYJ-48 gear-reduction stepper motor (small)
  X113647 Stepper Driver Board: A common stepper motor driver board based on ULN2003APG darlington array
